# Fritzing sketch coche (saved by Fritzing 0.9.3b)
breadboards: 1

parts:
  Componente1 = Arduino Uno (Rev3)
  R1 = Resistor [tolerance=±5% resistance=220 package=THT]
  JP1 = Header 6 [package=1x06-smd]
  S1 = Pushbutton [package="[THT]"]
  R2 = Resistor [tolerance=±5% resistance=10k package=THT]
  U3 = RELAY [package=relay-jzc]
  LED1 = LED - 5mm [color="Red (633nm)" package="5 mm [THT]"]
  U4 = TCM8240MD [package=tcm8240md]

nets:
  N1: Componente1.D8, JP1.2
  N2: Componente1.D9_PWM, R1.Pin_0, JP1.3, U3.NO
  N3: Componente1.D2, JP1.5, S1.Pin_1, S1.Pin_2, R2.Pin_1
  N4: Componente1.5V, JP1.1, JP1.4, S1.Pin_3, S1.Pin_4, U3.COIL2
  N5: Componente1.GND, JP1.6, R2.Pin_0, U3.NC, LED1.cathode
  N6: R1.Pin_1, LED1.anode
  N7: U3.MAIN, U4.RESET
  N8: U3.COIL1, U4.PVDD(2.8V)

// code stored in the sketch: coche.ino
/*
Exploring Arduino - Code Listing 2-5: Debounced Button Toggling
http://www.exploringarduino.com/content/ch2

Copyright 2013 Jeremy Blum ( http://www.jeremyblum.com )
This program is free software: you can redistribute it and/or modify
it under the terms of the GNU General Public License v3 as published by
the Free Software Foundation.
*/

const int LED_ON=9;             //The LED is connected to pin 9
const int LED_OFF=8;             //The LED is connected to pin 9
const int BUTTON=2;          //The Button is connected to pin 2
boolean lastButton = LOW;    //Variable containing the previous button state
boolean currentButton = LOW; //Variable containing the current button state
boolean ledOn = false;       //The present state of the LED (on/off)

void setup() {
  pinMode (LED_ON, OUTPUT);     //Set the LED pin as an output
  pinMode (LED_OFF, OUTPUT);
  pinMode (BUTTON, INPUT);   //Set button as input (not required)
}

/*
* Debouncing Function
* Pass it the previous button state,
* and get back the current debounced button state.
*/
boolean debounce(boolean last) {
  boolean current = digitalRead(BUTTON);       //Read the button state
  if (last != current) {                         //if it's different?
    delay(5);                                  //wait 5ms
    current = digitalRead(BUTTON);             //read it again
  }
  return current;                              //return the current value
}

void loop() {
  currentButton = debounce(lastButton);              //read debounced state
  if (lastButton == LOW && currentButton == HIGH)    //if it was pressed?
    ledOn = !ledOn;                                  //toggle the LED value


  lastButton = currentButton;                        //reset button value

  digitalWrite(LED_ON, ledOn);                          //cambia led arriba
  digitalWrite(LED_OFF, !ledOn);										 //cambia led abajo
}
